# Fritzing sketch Pillow-Breadboard (saved by Fritzing 0.9.0b)
breadboards: 1

parts:
  Part1 = Arduino Uno (Rev3) - ICSP
  Part2 = DeuLigne 1.1 - The Snootlab's LCD shield for Arduino
  U1 = DS1307 [package=so08]
  M1 = DC Motor
  S1 = Round Pushbutton
  R1 = Resistor [tolerance=±5% resistance=10k package=THT]
  J1 = Piezo Speaker
  LED1 = smd LED [color="Blue (470nm)" package="1206 [SMD]"]
  R2 = Resistor [tolerance=±5% resistance=560 package=THT]
  Q1 = NPN-Transistor [package="TO92 [THT]"]
  D1 = Rectifier Diode [part_number=1N4001 package="300 mil [THT]"]
  R3 = Resistor [tolerance=±5% resistance=2.2k package=THT]

nets:
  N1: Part1.A0, Part2.A0
  N2: Part1.A4/SDA, U1.SCL
  N3: Part1.A5/SCL, U1.SDA
  N4: Part1.RESET, Part2.RESET
  N5: Part1.D8, Part2.D8
  N6: Part1.D9_PWM, Part2.D9
  N7: Part1.D10_PWM/SS, Part2.D10_SS
  N8: Part1.D13/SCK, LED1.anode
  N9: Part1.D2, S1.leg0, R1.Pin_1
  N10: Part1.D3_PWM, J1.pin2
  N11: Part1.D4, Part2.D4
  N12: Part1.D5_PWM, Part2.D5
  N13: Part1.D6_PWM, Part2.D6
  N14: Part1.D7, Part2.D7
  5V: Part1.5V, Part2.+5V, U1.VCC, M1.pin_1, S1.leg1, D1.cathode
  GND: Part1.GND, Part2.GND, U1.GND, R1.Pin_0, J1.pin1, R2.Pin_0, Q1.C
  VIN: Part1.VIN, Part2.VIN
  N15: M1.pin_2, Q1.E, D1.anode
  N16: LED1.cathode, R2.Pin_1
  N17: Q1.B, R3.Pin_0
